# Fritzing sketch tryAgainWifiRelayMotor (saved by Fritzing 0.9.10b)
circuit board: 10.7056cm x 8.59836cm
breadboards: 1

parts:
  LOGIC_LEVEL_SHIFTER = 74AHCT125 [part_number=SN74AHCT125 package=dil14]
  FEATHER_ESP32 = Adafruit HUZZAH32 ESP32 Feather [part_number="Adafruit #3405"]
  buck_converter = Adafruit MPM3610 5V
  VIN = Power Jack [package=power_jack_combo]
  MOTORWING = Adafruit DC+Stepper FeatherWing [part_number="Adafruit #2927"]
  M1 = Power Jack [package=power_jack_combo]
  M2 = Power Jack [package=power_jack_combo]
  M3 = Power Jack [package=power_jack_combo]
  M4 = Power Jack [package=power_jack_combo]
  RELAI_1/2 = 2RelayModule
  RELAI_3/4 = 2RelayModule
  proto = Adafruit FeatherWing Proto [part_number="Adafruit #2884"]
  LOGIC_LEVEL_SHIFTER1 = 74AHCT125 [part_number=SN74AHCT125 package=dil14]
  LOGIC_LEVEL_SHIFTER2 = 74AHCT125 [part_number=SN74AHCT125 package=dil14]
  Composant2 = Adafruit 4-channel I2C-safe Bi-directional Logic Level Converter [part_number="Adafruit #757"]
  proto1 = Adafruit FeatherWing Proto [part_number="Adafruit #2884"]

nets:
  GND: LOGIC_LEVEL_SHIFTER.1OE, LOGIC_LEVEL_SHIFTER.2OE, LOGIC_LEVEL_SHIFTER.GND, LOGIC_LEVEL_SHIFTER.3OE, LOGIC_LEVEL_SHIFTER.4OE, FEATHER_ESP32.GND, buck_converter.GND, VIN.GND, MOTORWING.GND, RELAI_1/2.GND, RELAI_3/4.GND
  N1: LOGIC_LEVEL_SHIFTER.1A, FEATHER_ESP32.IO13_A12
  N2: LOGIC_LEVEL_SHIFTER.1Y, RELAI_1/2.IN1
  N3: LOGIC_LEVEL_SHIFTER.2A, FEATHER_ESP32.IO12_A11
  N4: LOGIC_LEVEL_SHIFTER.2Y, RELAI_1/2.IN2
  N5: LOGIC_LEVEL_SHIFTER.3Y, RELAI_3/4.IN1
  N6: LOGIC_LEVEL_SHIFTER.3A, FEATHER_ESP32.IO27_A10
  N7: LOGIC_LEVEL_SHIFTER.4Y, RELAI_3/4.IN2
  N8: LOGIC_LEVEL_SHIFTER.4A, FEATHER_ESP32.IO33_A9
  VCC: LOGIC_LEVEL_SHIFTER.VCC, FEATHER_ESP32.VBUS, buck_converter.5.0V, RELAI_1/2.VCC, RELAI_3/4.VCC
  3.3V: FEATHER_ESP32.3.3V, MOTORWING.+3.3V
  N9: FEATHER_ESP32.SCL, MOTORWING.SCL
  N10: FEATHER_ESP32.SDA, MOTORWING.SDA
  N11: buck_converter.VIN, VIN.PWR, MOTORWING.VMOTOR
  N12: MOTORWING.M1B, M1.GND
  N13: MOTORWING.M1A, M1.PWR
  N14: MOTORWING.M2A, M2.GND
  N15: MOTORWING.M2B, M2.PWR
  N16: MOTORWING.M3B, M3.PWR
  N17: MOTORWING.M3A, M3.GND
  N18: MOTORWING.M4A, M4.PWR
  N19: MOTORWING.M4B, M4.GND
  N20: proto.USB, LOGIC_LEVEL_SHIFTER1.VCC
  N21: proto.N, LOGIC_LEVEL_SHIFTER1.1A
  N22: proto.M, LOGIC_LEVEL_SHIFTER1.2A
  N23: proto.L, LOGIC_LEVEL_SHIFTER1.3A
  N24: proto.K, LOGIC_LEVEL_SHIFTER1.4A
  GND_2: proto.GND, LOGIC_LEVEL_SHIFTER1.1OE, LOGIC_LEVEL_SHIFTER1.2OE, LOGIC_LEVEL_SHIFTER1.GND, LOGIC_LEVEL_SHIFTER1.3OE, LOGIC_LEVEL_SHIFTER1.4OE
  N25: proto.N$36, LOGIC_LEVEL_SHIFTER1.1Y
  N26: proto.N$37, LOGIC_LEVEL_SHIFTER1.2Y
  N27: proto.N$42, LOGIC_LEVEL_SHIFTER1.3Y
  N28: proto.N$43, LOGIC_LEVEL_SHIFTER1.4Y
  N29: LOGIC_LEVEL_SHIFTER2.1OE, LOGIC_LEVEL_SHIFTER2.2OE, LOGIC_LEVEL_SHIFTER2.GND, LOGIC_LEVEL_SHIFTER2.3OE, LOGIC_LEVEL_SHIFTER2.4OE
  GND_3: Composant2.GND, proto1.GND, proto1.N$32
  N30: Composant2.A4, proto1.N
  N31: Composant2.A3, proto1.USB
  N32: Composant2.A2, proto1.EN
  N33: Composant2.A1, proto1.VBAT
  N34: Composant2.LV, proto1.3V
  N35: Composant2.B4, proto1.N$47
  N36: Composant2.B3, proto1.N$44
  N37: Composant2.B2, proto1.N$41
  N38: Composant2.B1, proto1.N$38
  N39: Composant2.HV, proto1.N$31

custom parts:
  74AHCT125: Quad Level-Shifter (3V to 5V) Quadruple Bus Buffer Gates With 3-State Outputs
  Adafruit DC+Stepper FeatherWing: This is the DC Motor + Stepper FeatherWing which will let you use 2 x bi-polar stepper motors or 4 x brushed DC motorx (or 1 stepper and 2 DC motors). Using our Feather Stacking Headers or Feather Female Headers you can connect a FeatherWing on top or bottom of your Feather board and let the board take flight! The original Adafruit Motorshield Kit is one of our most beloved kits, which is why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
  2RelayModule: 2 relay arduino module SONGLE SRD05VDC-SL-C
  Adafruit FeatherWing Proto: This is the FeatherWing Proto - a prototyping add-on for all Feather boards. Using our Feather Stacking Headers or Feather Female Headers you can connect a FeatherWing on top or bottom of your Feather board and let the board take flight! This has a duplicate breakout for each pin on a Feather, as well as a bunch of plain grid proto holes. For GND and 3.3V, we give you a strip of connected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
  Adafruit 4-channel I2C-safe Bi-directional Logic Level Converter: Because the Arduino (and Basic Stamp) are 5V devices, and most modern sensors, displays, flash cards and modes are 3.3V-only, many makers find that they need to perform level shifting/conversion to protect the 3.3V device from 5V. We do have some other handy level shifters in the shop, from the DIP 74LVC245 to the fancy bi-directional TXB0108. However, neither of these are happy to work with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
