# Fritzing sketch tryAgainWifiRelayMotorLLS (saved by Fritzing 0.9.10b)
breadboards: 1

parts:
  proto2 = Adafruit FeatherWing Proto [part_number="Adafruit #2884"]
  LOGIC_LEVEL_SHIFTER3 = 74AHCT125 [part_number=SN74AHCT125 package=dil14]
  LOGIC_LEVEL_SHIFTER4 = 74AHCT125 [part_number=SN74AHCT125 package=dil14]
  Composant4 = Adafruit 4-channel I2C-safe Bi-directional Logic Level Converter [part_number="Adafruit #757"]
  proto3 = Adafruit FeatherWing Proto [part_number="Adafruit #2884"]

nets:
  N1: proto2.USB, LOGIC_LEVEL_SHIFTER3.VCC
  N2: proto2.L, LOGIC_LEVEL_SHIFTER3.3A
  N3: proto2.K, LOGIC_LEVEL_SHIFTER3.4A
  GND: proto2.GND, LOGIC_LEVEL_SHIFTER3.1OE, LOGIC_LEVEL_SHIFTER3.2OE, LOGIC_LEVEL_SHIFTER3.GND, LOGIC_LEVEL_SHIFTER3.3OE, LOGIC_LEVEL_SHIFTER3.4OE
  N4: proto2.N$36, LOGIC_LEVEL_SHIFTER3.1Y
  N5: proto2.N$37, LOGIC_LEVEL_SHIFTER3.2Y
  N6: proto2.N$42, LOGIC_LEVEL_SHIFTER3.3Y
  N7: proto2.N$43, LOGIC_LEVEL_SHIFTER3.4Y
  N8: LOGIC_LEVEL_SHIFTER4.1OE, LOGIC_LEVEL_SHIFTER4.2OE, LOGIC_LEVEL_SHIFTER4.GND, LOGIC_LEVEL_SHIFTER4.3OE, LOGIC_LEVEL_SHIFTER4.4OE
  GND_2: Composant4.GND, proto3.GND, proto3.N$32
  N9: Composant4.A4, proto3.N
  N10: Composant4.A3, proto3.USB
  N11: Composant4.A2, proto3.EN
  N12: Composant4.A1, proto3.VBAT
  N13: Composant4.LV, proto3.3V
  N14: Composant4.B4, proto3.N$47
  N15: Composant4.B3, proto3.N$44
  N16: Composant4.B2, proto3.N$41
  N17: Composant4.B1, proto3.N$38
  N18: Composant4.HV, proto3.N$31

custom parts:
  Adafruit FeatherWing Proto: This is the FeatherWing Proto - a prototyping add-on for all Feather boards. Using our Feather Stacking Headers or Feather Female Headers you can connect a FeatherWing on top or bottom of your Feather board and let the board take flight! This has a duplicate breakout for each pin on a Feather, as well as a bunch of plain grid proto holes. For GND and 3.3V, we give you a strip of connected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
  74AHCT125: Quad Level-Shifter (3V to 5V) Quadruple Bus Buffer Gates With 3-State Outputs
  Adafruit 4-channel I2C-safe Bi-directional Logic Level Converter: Because the Arduino (and Basic Stamp) are 5V devices, and most modern sensors, displays, flash cards and modes are 3.3V-only, many makers find that they need to perform level shifting/conversion to protect the 3.3V device from 5V. We do have some other handy level shifters in the shop, from the DIP 74LVC245 to the fancy bi-directional TXB0108. However, neither of these are happy to work with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
